// Logisim project projet.circ as structural Verilog: 2 circuits, main circuit main
module main (
);

  \Unité_de_calcul  \unité_de_calcul_1  ();  // open: A, B, in_3, in_4, Code_opé, D, S
endmodule

module \Unité_de_calcul  (
  input  [7:0] A,
  input  [7:0] B,
  input  [1:0] in_3,
  input  in_4,
  input  [1:0] \Code_opé ,
  output D,
  output [7:0] S
);

  wire adder_1_cout, and_1_out, and_2_out, and_3_out, and_4_out, comparator_1_eq, comparator_2_eq, not_1_out,
       not_2_out, not_3_out, not_4_out, not_5_out;
  wire [3:0] multiplier_2_out;
  wire [7:0] adder_1_out, divider_1_out, multiplier_1_out, subtractor_1_out;

  not not_1 (not_1_out, \Code_opé [1]);
  not not_2 (not_2_out, \Code_opé [0]);
  and and_1 (and_1_out, not_2_out, not_1_out);
  not not_3 (not_3_out, \Code_opé [1]);
  and and_2 (and_2_out, \Code_opé [0], not_3_out);
  not not_4 (not_4_out, \Code_opé [0]);
  and and_3 (and_3_out, not_4_out, \Code_opé [1]);
  Adder adder_1 (.a(A), .b(B), .out(adder_1_out), .cout(adder_1_cout));  // open: cin
  Subtractor subtractor_1 (.a(A), .b(B), .out(subtractor_1_out));  // open: bin, bout
  and and_4 (and_4_out, \Code_opé [0], \Code_opé [1]);
  Multiplier multiplier_1 (.a(A), .b(B), .out(multiplier_1_out));  // open: cin, cout
  Divider divider_1 (.a(A), .b(B), .out(divider_1_out));  // open: upper, rem
  Multiplier #(.width(4)) multiplier_2 (.a(A[7:4]), .b(B[7:4]), .out(multiplier_2_out));  // open: cin, cout
  Comparator comparator_1 (.a(B), .b({8{1'b0}}), .eq(comparator_1_eq));  // open: gt, lt
  Comparator #(.width(4)) comparator_2 (.a(multiplier_2_out), .b(4'b0000), .eq(comparator_2_eq));  // open: gt, lt
  not not_5 (not_5_out, comparator_2_eq);
  Multiplexer #(.select(2), .width(8)) multiplexer_1 (
    .in0(adder_1_out), .in1(subtractor_1_out), .in2(multiplier_1_out), .in3(divider_1_out), .out(S),
    .sel(in_3), .en(in_4));
  Multiplexer #(.select(2)) multiplexer_2 (
    .in0(adder_1_cout), .in1(1'b0), .in2(not_5_out), .in3(comparator_1_eq), .out(D), .sel(in_3), .en(in_4));

  // Notes on the sheet:
  //   Addition
  //   Soustraction
  //   en valeur absolue
  //   Multiplication
  //   Overflow impossible
  //   with 2 unsigned int
  //   Division entière
  //   Result *
  //   Overflow *
  //   Result +
  //   Overflow +
  //   Result /
  //   Overflow /
  //   Result -
  //   S : sortie du calcul
  //   A, B : Paramètres du calcul
  //   D : Indication si le résultat a débordé
  //   Code opé : Code d'opération (00+, 01-, 10*, 11/)
endmodule
